// Logisim project Design_Project_FA21_Ver_2.circ as structural Verilog: 5 circuits, main circuit main
module main (
  input  in_1,
  input  set_to_1,
  output [6:0] out_3,
  output out_4
);

  wire and_1_out, CLK, flipdetector_1_flipdetected;
  wire [1:0] count_3_flips_1_q2;
  wire [6:0] switch_circuit_1_channel_out;

  Clock clock_1 (.out(CLK));
  Keyboard keyboard_1 (.clk(CLK), .re(set_to_1), .clr(in_1), .avail(out_4), .data(out_3));
  LED led_1 (.in(out_4));
  flipDetector flipdetector_1 (
    .in_1(out_3), .Reset(in_1), .Enable(set_to_1), .CLK(CLK), .FLIPdetected(flipdetector_1_flipdetected));
  Switch_Circuit switch_circuit_1 (
    .Channel_OUT(switch_circuit_1_channel_out), .flip(flipdetector_1_flipdetected), .CLK(CLK), .Reset(in_1),
    .Channel_IN(out_3));
  LED led_2 (.in(flipdetector_1_flipdetected));
  TTY #(.cols(80)) tty_1 (.data(out_3), .clk(CLK), .we(set_to_1), .clr(in_1));
  TTY #(.cols(80)) tty_2 (.data(switch_circuit_1_channel_out), .clk(CLK), .we(set_to_1), .clr(in_1));
  Hex_Digit_Display hex_digit_display_1 (.value({2'b00, count_3_flips_1_q2}));  // open: dp
  count_3_FLIPS count_3_flips_1 (
    .flip_IN(flipdetector_1_flipdetected), .CLK(CLK), .RESET(in_1), .q1(count_3_flips_1_q2[1]),
    .q2(count_3_flips_1_q2[0]));
  and and_1 (and_1_out, count_3_flips_1_q2[1], count_3_flips_1_q2[0]);
  LED led_3 (.in(and_1_out));

  // Other names for the same wires on the sheet: ENABLE = set_to_1; RESET = in_1

  // Notes on the sheet:
  //   Version 2 
  //   set to 1 to read character
  //   set to 1 then back to 0 to empty buffer
  //   System Clock
  //   set to 1 then back to 0
  //   Check Channel Bits
  //   Red Light is on at each " flip " 
  //   set to 1 then back to 0 to Clear Screen
  //   set to 1 to write enable
  //   Normal Text
  //   Letters switched from lower case to upper case and viceversa
  //   Blue Light is On after 3 Instances of a  " flip "
endmodule

module Sub_Add_Comporator (
  input  [6:0] Channel_IN,
  output [6:0] Channel_OUT
);

  wire comparator_1_gt, comparator_2_lt, comparator_3_gt, comparator_4_lt, comparator_5_gt, comparator_5_lt,
       not_1_out, not_2_out, or_1_out, xnor_1_out, xnor_2_out;
  wire [1:0] adder_1_cout;
  wire [6:0] adder_1_out, multiplexer_1_out, subtractor_1_out;

  Comparator #(.mode("unsigned"), .width(7)) comparator_1 (
    .a(Channel_IN), .b(7'b1000000), .gt(comparator_1_gt));  // open: eq, lt
  Comparator #(.mode("unsigned"), .width(7)) comparator_2 (
    .a(Channel_IN), .b(7'b1011011), .lt(comparator_2_lt));  // open: gt, eq
  Comparator #(.mode("unsigned"), .width(7)) comparator_3 (
    .a(Channel_IN), .b(7'b1100000), .gt(comparator_3_gt));  // open: eq, lt
  Comparator #(.mode("unsigned"), .width(7)) comparator_4 (
    .a(Channel_IN), .b(7'b1111011), .lt(comparator_4_lt));  // open: gt, eq
  Comparator #(.mode("unsigned"), .width(7)) comparator_5 (
    .a(Channel_IN), .b(7'b1100000), .gt(comparator_5_gt), .lt(comparator_5_lt));  // open: eq
  xnor xnor_1 (xnor_1_out, comparator_1_gt, comparator_2_lt);
  xnor xnor_2 (xnor_2_out, comparator_3_gt, comparator_4_lt);
  or or_1 (or_1_out, xnor_1_out, xnor_2_out);
  not not_1 (not_1_out, comparator_5_gt);
  Subtractor #(.width(7)) subtractor_1 (
    .a(Channel_IN), .b(7'b0100000), .out(subtractor_1_out), .bin(not_1_out), .bout(adder_1_cout[1]));
  not not_2 (not_2_out, comparator_5_lt);
  Adder #(.width(7)) adder_1 (
    .a(Channel_IN), .b(7'b0100000), .out(adder_1_out), .cin(not_2_out), .cout(adder_1_cout[0]));
  Multiplexer #(.enable("false"), .select(2), .width(7)) multiplexer_1 (
    .in0(adder_1_out), .in1(subtractor_1_out), .in2({7{1'b0}}), .in3({7{1'b0}}), .out(multiplexer_1_out),
    .sel(adder_1_cout));
  Multiplexer #(.enable("false"), .width(7)) multiplexer_2 (
    .in0(Channel_IN), .in1(multiplexer_1_out), .out(Channel_OUT), .sel(or_1_out));

  // Notes on the sheet:
  //   64 to 91 or 96 to 123
  //   This will identify if the letters are between the range of
  //   This is the Adder and Subtractor that will make the change from upper case to lower case and vice versa
  //   Will pass the input selected, if it's not a letter like a sign the 0 will activate in MUX
endmodule

module Switch_Circuit (
  input  [6:0] Channel_IN,
  input  flip,
  input  CLK,
  input  Reset,
  output [6:0] Channel_OUT
);

  wire t_ff_1_q;
  wire [6:0] sub_add_comporator_1_channel_out;

  T_Flip_Flop #(.trigger("falling")) t_ff_1 (.T(flip), .clk(CLK), .Q(t_ff_1_q), .reset(Reset));  // open: Qn, preset
  Sub_Add_Comporator sub_add_comporator_1 (.Channel_OUT(sub_add_comporator_1_channel_out), .Channel_IN(Channel_IN));
  Multiplexer #(.enable("false"), .width(7)) multiplexer_1 (
    .in0(Channel_IN), .in1(sub_add_comporator_1_channel_out), .out(Channel_OUT), .sel(t_ff_1_q));

  // Notes on the sheet:
  //   This T type flip flop will toggle when it enters 1 when flip is activated
  //   This is the Sub_Add_Comparator will provide the change of the letter and let any sign pass. 
endmodule

module flipDetector (
  input  [6:0] in_1,
  input  Reset,
  input  Enable,
  input  CLK,
  output FLIPdetected
);

  wire comparator_1_eq, comparator_2_eq, comparator_3_eq, comparator_4_eq, comparator_5_eq, comparator_6_eq,
       comparator_7_eq, comparator_8_eq, comparator_9_eq, comparator_10_eq, or_1_out, or_2_out, or_3_out,
       or_4_out;
  wire [6:0] register_1_q, register_2_q, register_3_q, register_4_q, register_5_q, register_6_q;

  Register #(.width(7)) register_1 (.D(in_1), .en(Enable), .clk(CLK), .Q(register_1_q), .clr(Reset));
  Register #(.width(7)) register_2 (.D(register_1_q), .en(Enable), .clk(CLK), .Q(register_2_q), .clr(Reset));
  Register #(.width(7)) register_3 (.D(register_2_q), .en(Enable), .clk(CLK), .Q(register_3_q), .clr(Reset));
  Register #(.width(7)) register_4 (.D(register_3_q), .en(Enable), .clk(CLK), .Q(register_4_q), .clr(Reset));
  Register #(.width(7)) register_5 (.D(register_4_q), .en(Enable), .clk(CLK), .Q(register_5_q), .clr(Reset));
  Register #(.width(7)) register_6 (.D(register_5_q), .en(Enable), .clk(CLK), .Q(register_6_q), .clr(Reset));
  Comparator #(.width(7)) comparator_1 (.a(7'b0100000), .b(register_1_q), .eq(comparator_1_eq));  // open: gt, lt
  Comparator #(.width(7)) comparator_2 (.a(7'b1010000), .b(register_2_q), .eq(comparator_2_eq));  // open: gt, lt
  Comparator #(.width(7)) comparator_3 (.a(register_2_q), .b(7'b1110000), .eq(comparator_3_eq));  // open: gt, lt
  Comparator #(.width(7)) comparator_4 (.a(7'b1001001), .b(register_3_q), .eq(comparator_4_eq));  // open: gt, lt
  Comparator #(.width(7)) comparator_5 (.a(register_3_q), .b(7'b1101001), .eq(comparator_5_eq));  // open: gt, lt
  Comparator #(.width(7)) comparator_6 (.a(7'b1001100), .b(register_4_q), .eq(comparator_6_eq));  // open: gt, lt
  Comparator #(.width(7)) comparator_7 (.a(register_4_q), .b(7'b1101100), .eq(comparator_7_eq));  // open: gt, lt
  Comparator #(.width(7)) comparator_8 (.a(7'b1000110), .b(register_5_q), .eq(comparator_8_eq));  // open: gt, lt
  Comparator #(.width(7)) comparator_9 (.a(register_5_q), .b(7'b1100110), .eq(comparator_9_eq));  // open: gt, lt
  Comparator #(.width(7)) comparator_10 (.a(7'b0100000), .b(register_6_q), .eq(comparator_10_eq));  // open: gt, lt
  or or_1 (or_1_out, comparator_2_eq, comparator_3_eq);
  or or_2 (or_2_out, comparator_4_eq, comparator_5_eq);
  or or_3 (or_3_out, comparator_6_eq, comparator_7_eq);
  or or_4 (or_4_out, comparator_8_eq, comparator_9_eq);
  and and_1 (FLIPdetected, comparator_1_eq, or_1_out, or_2_out, or_3_out, or_4_out, comparator_10_eq);
endmodule

module count_3_FLIPS (
  input  flip_IN,
  input  CLK,
  input  RESET,
  output q1,
  output q2
);

  wire and_1_out, and_2_out, and_3_out, d_ff_2_qn, or_1_out, or_2_out, xor_1_out, xor_2_out;

  xor xor_1 (xor_1_out, q1, flip_IN);
  and and_1 (and_1_out, q1, d_ff_2_qn);
  or or_1 (or_1_out, and_1_out, and_2_out);
  and and_2 (and_2_out, ~d_ff_2_qn, xor_1_out);  // AND_Gate
  and and_3 (and_3_out, q1, flip_IN);
  or or_2 (or_2_out, and_3_out, xor_2_out);
  xor xor_2 (xor_2_out, ~d_ff_2_qn, flip_IN);  // XOR_Gate
  D_Flip_Flop d_ff_1 (.D(or_1_out), .clk(CLK), .Q(q1), .reset(RESET));  // open: Qn, preset
  D_Flip_Flop d_ff_2 (.D(or_2_out), .clk(CLK), .Q(q2), .Qn(d_ff_2_qn), .reset(RESET));  // open: preset
endmodule
